# Fritzing sketch RFIDReader (saved by Fritzing 0.9.3b)
circuit board: 5.5cm x 6.50692cm
breadboards: 1

parts:
  R16 = Resistor [tolerance=±5% resistance=10k package=THT]
  C2 = Electrolytic Capacitor [capacitance=0.1nF package="100 mil [THT, electrolytic]"]
  C5 = Ceramic Capacitor [capacitance=100nF package="100 mil [THT, multilayer]"]
  HLK-PM1 = HLK-PM01
  J-PRG = screw terminal, 5 pins
  R24 = Resistor [tolerance=±5% resistance=10k package=THT]
  F1 = Resettable Fuse PTC [package=ptc]
  F2 = Resettable Fuse PTC [package=ptc]
  U5 = ESP-12F (ESP8266 WiFi Module) [part_number=ESP8266]
  J-RC522 = screw terminal, 8 pins
  SG2 = Buzzer 12mm [package=buzzer-12mm]
  J-AC = screw terminal, 2 pins
  R25 = Resistor [tolerance=±5% resistance=10k package=THT]

nets:
  RST: R16.Pin_0, J-PRG.pin4, U5.RST
  3.3V: R16.Pin_1, C2.+, C5.1, HLK-PM1.+Vo, R24.Pin_1, U5.VCC, U5.EN, J-RC522.pin8, R25.Pin_1
  GND: C2.-, C5.0, HLK-PM1.-Vo, J-PRG.pin5, U5.GND, U5.GPIO15, J-RC522.pin6, SG2.2
  N1: HLK-PM1.AC#0, F1.1, F2.2
  N2: HLK-PM1.AC#1, F1.2, J-AC.pin1
  DTR: J-PRG.pin1, R24.Pin_0, U5.GPIO0
  N3: J-PRG.pin2, U5.TXD0
  N4: J-PRG.pin3, U5.RXD0
  N5: F2.1, J-AC.pin2
  N6: U5.GPIO2, R25.Pin_0
  N7: U5.GPIO4, J-RC522.pin1
  N8: U5.GPIO16, SG2.1
  N9: U5.GPIO14, J-RC522.pin2
  N10: U5.GPIO12, J-RC522.pin4
  N11: U5.GPIO13, J-RC522.pin3

notes:
  AC
  RFID Reader V1.1
  JD 020520

custom parts:
  HLK-PM01: AC-DC 220V to 5V Step-Down Power Supply Module
  ESP-12F (ESP8266 WiFi Module): WiFi Module based on the ESP8266 with onboard PCB antenna and UART communications
